# Fritzing sketch TeensyAASS (saved by Fritzing 0.9.3b)
circuit board: 4.5cm x 6.5cm
breadboards: 1

parts:
  J1 = female pin header, 14 pins [form="♀ (female)"]
  J2 = female pin header, 14 pins [form="♀ (female)"]
  R1 = Rotary Potentiometer (Small) [maximum_resistance=100kΩ package=THT]
  R2 = Rotary Potentiometer (Small) [maximum_resistance=100kΩ package=THT]
  LED1 = LED - 5mm [color="Red (633nm)" package="5 mm [THT]"]
  S1 = Toggle Switch [package=THT]
  R4 = Resistor [tolerance=±5% resistance=1k package="2010 [SMD]"]
  R3 = Resistor [tolerance=±5% resistance=47 package="2010 [SMD]"]

nets:
  N1: J1.pin3, R1.leg1, R2.leg1, R4.Pin_1
  N2: J1.pin10, R2.wiper
  N3: J1.pin11, R1.wiper
  N4: J2.pin1, R1.leg2, R2.leg2, S1.COM, R3.Pin_1
  N5: J2.pin7, S1.L1, R4.Pin_0
  N6: J2.pin10, LED1.anode
  N7: LED1.cathode, R3.Pin_0
